# Fritzing sketch schematics_base (saved by Fritzing 1.0.7)
breadboards: 1

parts:
  Lora32 = Heltec WiFi Kit 32 V3 [part_number=HTIT-WB32_V3]
  GPS_Module = GT-U8-GPS module
  BMP280_Breakout2 = Barometric Pressure Sensor - BMP180 Breakout (GY-68)

nets:
  N1: Lora32.pin_6, GPS_Module.Pin_3
  N2: Lora32.pin_16, Lora32.pin_17, GPS_Module.Pin_1, BMP280_Breakout2.VCC
  N3: Lora32.pin_18, Lora32.pin_19, GPS_Module.Pin_2, BMP280_Breakout2.GND
  N4: Lora32.pin_21, Lora32.pin_22
  N5: Lora32.pin_31, BMP280_Breakout2.SDA
  N6: Lora32.pin_32, BMP280_Breakout2.SCL

custom parts:
  Heltec WiFi Kit 32 V3: The Heltec WiFi Kit 32 (V3) is an IoT development board designed and produced by Heltec Automation and based on the Espressif ESP32 processor module. The board includes WiFi and Bluetooth/BLE functions, as well as a 0.96″ OLED display and a Li-Po battery management system. Links: Heltec WiFi Kit 32 (V3) product page Github
  GT-U8-GPS module: GPS / BDS W/GT-U8 WITH CERAMIC ANTENNA.
