# Fritzing sketch schematics_plane (saved by Fritzing 1.0.7)
breadboards: 2

parts:
  Part1 = Arduino Nano (Rev3.0)
  U1 = TRANSISTOR_NPN_2 [package=to-92]
  R1 = Resistor [tolerance=±5% resistance=220 package="1206 [SMD]"]
  R2 = Resistor [tolerance=±5% resistance=220 package="1206 [SMD]"]
  J1 = Dagu DGServo 9g header (male) [package=THT]
  Part2 = I2C level shifter bidirectional
  Mod1 = Heltec WiFi Kit 32 V3 [part_number=HTIT-WB32_V3]
  A1 = GT-U8-GPS module
  BMP280_Breakout1 = BMP280 Breakout Board [part_number=BMP280]
  Part3 = InvenSense MPU6050
  Part4 = HMC5883L Triple-axis Magnetometer [part_number=1746]

nets:
  N1: Part1.D0/RX, U1.E, R1.Pin_0
  GND: Part1.GND, U1.C, J1.gnd, Part2.GND, Mod1.pin_18, Mod1.pin_19, A1.Pin_2, BMP280_Breakout1.GND, Part3.GND, Part4.GND
  5V: Part1.5V, R1.Pin_1, J1.Vcc, Part2.HV, Mod1.pin_20
  N2: Part1.A5, Part2.HV4
  N3: Part1.A4, Part2.HV3
  N4: U1.B, R2.Pin_1
  N5: R2.Pin_0, J1.pulse
  N6: Part2.LV4, Mod1.pin_32, BMP280_Breakout1.SCL, Part3.SCL, Part4.SCL
  N7: Part2.LV3, Mod1.pin_31, BMP280_Breakout1.SDA, Part3.SDA, Part4.SDA
  VCC: Part2.LV, Mod1.pin_16, Mod1.pin_17, A1.Pin_1, BMP280_Breakout1.VCC, Part3.VCC, Part4.VIN
  N8: Mod1.pin_6, A1.Pin_3
  N9: Mod1.pin_21, Mod1.pin_22

custom parts:
  Heltec WiFi Kit 32 V3: The Heltec WiFi Kit 32 (V3) is an IoT development board designed and produced by Heltec Automation and based on the Espressif ESP32 processor module. The board includes WiFi and Bluetooth/BLE functions, as well as a 0.96″ OLED display and a Li-Po battery management system. Links: Heltec WiFi Kit 32 (V3) product page Github
  GT-U8-GPS module: GPS / BDS W/GT-U8 WITH CERAMIC ANTENNA.
  BMP280 Breakout Board: This is a breakout board for the Bosch Sensortec BMP280, "an absolute barometric pressure sensor especially designed for mobile applications." The operation range is 300 to 1100 hPa. Supply voltage is 1.2 to 3.6V. Operating temperature range is -40 to +85 °C.
